// Logisim project TAHX_TOP_logisim.circ as structural Verilog: 9 circuits, main circuit TAHX_TOP
module TAHX_TOP (
);

  wire undriven;

  fetch fetch_1 ();  // open: i_fault_i, i_ready_i, predict_pc_i, decode_stop_i, consume_i, window_count_o, window_o, recovery_valid_i, halt_i, reset_i, clk_i, icache_invalidate_i, recovery_pc_i, window_fault_o, window_pc_o, consumed_bytes_i, predict_valid_i, i_req_o, i_rvalid_i, i_addr_o, i_rdata_i
  decode_predict decode_predict_1 ();  // open: consume_o, window_count_i, window_i, reset_i, recovery_i, retire_i, clk_i, window_fault_i, window_pc_i, consumed_bytes_o, stop_o, predict_valid_o, predict_pc_o, out_ready_i, out_valid_o, out_count_o, out_block_o
  decode_queue decode_queue_1 ();  // open: flush_i, push_count_i, push_ready_o, reset_i, clk_i, push_valid_i, push_block_i, pop_take_i, pop_slot_o
  data_cache data_cache_1 (.reset_i(undriven));  // open: d_rdata_i, d_ready_i, d_addr_o, d_req_o, d_write_o, d_wdata_o, d_rvalid_i, d_fault_i, clk_i, stack_req_i, stack_ready_o, stack_rsp_o, exec_req_i, exec_ready_o, exec_rsp_o
  stack_unit stack_unit_1 ();  // open: clk_i, disp_wdata_i, disp_we_i, sync_dsp_i, lim_rsp_i, maint_i, mem_rsp_i, mem_req_o, disp_sel_i, frame_dsp_o, issue_o, issue_valid_o, decode_take_o, decode_slot_i, issue_ready_i, complete_i, frame_rsp_o, disp_o, mem_ready_i, maint_done_o, lim_dsp_i, sync_valid_i, sync_rsp_i, disp_wsel_i, reset_i, commit_o, idle_o, decode_valid_i
  exec_arith exec_arith_1 ();  // open: complete_fault_o, complete_result_valid_o, ready_o, reset_i, clk_i, complete_valid_o, complete_result_o, sync_valid_i, issue_valid_i, issue_class_i, issue_op_i, issue_a_i, issue_b_i, issue_c_i
  system system_1 ();  // open: resume_pc_i, halt_cause_o, halt_req_i, irq_ack_o, boot_block_i, copile_i, mem_rsp_i, mem_req_o, redirect_valid_o, boundary_pc_i, fault_i, fault_valid_i, disp_wsel_o, sync_rsp_o, sync_valid_o, stack_maint_o, disp_sel_o, frame_dsp_i, issue_i, issue_valid_i, reset_i, clk_i, issue_ready_o, complete_o, frame_rsp_i, disp_i, stack_maint_done_i, sync_dsp_o, disp_we_o, disp_wdata_o, fault_pc_i, boundary_valid_i, system_hold_o, redirect_pc_o, mem_ready_i, limits_o, sync_copile_o, irq_pending_i, irq_ack_code_o, halted_o, resume_req_i, halt_pc_o, exit_code_o, fpc_o, fcode_o, dr_o
  exec_entier exec_entier_1 (.reset_i(undriven));  // open: stack_maint_o, disp_sel_o, frame_dsp_i, issue_i, issue_valid_i, clk_i, issue_ready_o, complete_o, frame_rsp_i, disp_i, stack_maint_done_i, arith_ready_i, arith_complete_, mem_req_o, mem_ready_i, mem_rsp_i, limits_i, sync_valid_i, sync_copile_i, copile_o
endmodule

module fetch (
  input  reset_i,
  input  clk_i,
  input  halt_i,
  input  icache_invalidate_i,
  input  recovery_valid_i,
  input  recovery_pc_i,
  input  consume_i,
  input  consumed_bytes_i,
  input  decode_stop_i,
  input  predict_valid_i,
  input  predict_pc_i,
  input  i_ready_i,
  input  i_rvalid_i,
  input  i_fault_i,
  input  i_rdata_i,
  output window_o,
  output window_fault_o,
  output window_count_o,
  output window_pc_o,
  output i_req_o,
  output i_addr_o
);
endmodule

module decode_predict (
  input  recovery_i,
  input  retire_i,
  input  reset_i,
  input  clk_i,
  input  window_i,
  input  window_fault_i,
  input  window_count_i,
  input  window_pc_i,
  input  out_ready_i,
  output consume_o,
  output consumed_bytes_o,
  output stop_o,
  output predict_valid_o,
  output predict_pc_o,
  output out_valid_o,
  output out_count_o,
  output out_block_o
);
endmodule

module decode_queue (
  input  reset_i,
  input  clk_i,
  input  push_valid_i,
  input  push_count_i,
  input  push_block_i,
  input  flush_i,
  input  pop_take_i,
  output push_ready_o,
  output pop_slot_o
);
endmodule

module stack_unit (
  input  reset_i,
  input  sync_valid_i,
  input  clk_i,
  input  sync_dsp_i,
  input  issue_ready_i,
  input  sync_rsp_i,
  input  disp_we_i,
  input  complete_i,
  input  decode_slot_i,
  input  lim_dsp_i,
  input  disp_wsel_i,
  input  decode_valid_i,
  input  lim_rsp_i,
  input  disp_wdata_i,
  input  disp_sel_i,
  input  maint_i,
  input  mem_ready_i,
  input  mem_rsp_i,
  output issue_valid_o,
  output issue_o,
  output decode_take_o,
  output disp_o,
  output commit_o,
  output idle_o,
  output frame_rsp_o,
  output frame_dsp_o,
  output maint_done_o,
  output mem_req_o
);
endmodule

module data_cache (
  input  d_ready_i,
  input  d_rvalid_i,
  input  d_rdata_i,
  input  d_fault_i,
  input  reset_i,
  input  clk_i,
  input  stack_req_i,
  input  exec_req_i,
  output d_req_o,
  output d_write_o,
  output d_addr_o,
  output d_wdata_o,
  output stack_ready_o,
  output stack_rsp_o,
  output exec_ready_o,
  output exec_rsp_o
);
endmodule

module exec_entier (
  input  reset_i,
  input  clk_i,
  input  issue_valid_i,
  input  issue_i,
  input  frame_dsp_i,
  input  frame_rsp_i,
  input  disp_i,
  input  stack_maint_done_i,
  input  arith_ready_i,
  input  arith_complete_,
  input  mem_ready_i,
  input  mem_rsp_i,
  input  limits_i,
  input  sync_valid_i,
  input  sync_copile_i,
  output issue_ready_o,
  output complete_o,
  output disp_sel_o,
  output stack_maint_o,
  output mem_req_o,
  output copile_o
);
endmodule

module exec_arith (
  input  reset_i,
  input  clk_i,
  input  sync_valid_i,
  input  issue_valid_i,
  input  issue_class_i,
  input  issue_op_i,
  input  issue_a_i,
  input  issue_b_i,
  input  issue_c_i,
  output ready_o,
  output complete_valid_o,
  output complete_result_valid_o,
  output complete_result_o,
  output complete_fault_o
);
endmodule

module system (
  input  reset_i,
  input  boundary_pc_i,
  input  clk_i,
  input  issue_valid_i,
  input  issue_i,
  input  mem_ready_i,
  input  frame_dsp_i,
  input  mem_rsp_i,
  input  frame_rsp_i,
  input  copile_i,
  input  disp_i,
  input  boot_block_i,
  input  stack_maint_done_i,
  input  irq_pending_i,
  input  halt_req_i,
  input  resume_req_i,
  input  fault_valid_i,
  input  resume_pc_i,
  input  fault_pc_i,
  input  fault_i,
  input  boundary_valid_i,
  output fcode_o,
  output system_hold_o,
  output dr_o,
  output redirect_valid_o,
  output issue_ready_o,
  output redirect_pc_o,
  output mem_req_o,
  output complete_o,
  output limits_o,
  output disp_sel_o,
  output sync_copile_o,
  output stack_maint_o,
  output sync_valid_o,
  output irq_ack_o,
  output sync_dsp_o,
  output irq_ack_code_o,
  output sync_rsp_o,
  output disp_we_o,
  output halted_o,
  output disp_wsel_o,
  output halt_cause_o,
  output disp_wdata_o,
  output halt_pc_o,
  output exit_code_o,
  output fpc_o
);
endmodule
