// Logisim project TAHX_TOP_logisim_echelle_v11c.circ as structural Verilog: 10 circuits, main circuit TAHX_TOP
module TAHX_TOP (
);

  wire data_cache_1_p1, data_cache_1_p2, data_cache_1_p3, data_cache_1_p5, decode_predict_1_consume_o,
       decode_predict_1_out_valid_o, decode_predict_1_predict_valid_o, decode_predict_1_stop_o,
       decode_queue_1_push_ready_o, frontend_control_1_boundary_valid_o, frontend_control_1_recovery_valid_o,
       stack_unit_1_p1, stack_unit_1_p6, stack_unit_1_p7, stack_unit_1_p10, stack_unit_1_p11,
       stack_unit_1_p13, stack_unit_1_p15, stack_unit_1_p26, stack_unit_1_p29, system_1_halted_o,
       system_1_system_hold_o, undriven, undriven_2;
  wire [2:0] exec_arith_1_ready_o;
  wire [3:0] decode_predict_1_out_count_o, stack_unit_1_p19, stack_unit_1_p25;
  wire [5:0] decode_predict_1_consumed_bytes_o, fetch_1_window_count_o;
  wire [21:0] frontend_control_1_retire_o;
  wire [31:0] data_cache_1_p4, data_cache_1_p6, decode_predict_1_out_block_o, decode_predict_1_predict_pc_o,
       decode_queue_1_pop_slot_o, exec_arith_1_complete_valid_o, exec_entier_1_copile_o,
       fetch_1_window_fault_o, fetch_1_window_o, fetch_1_window_pc_o, frontend_control_1_boundary_pc_o,
       frontend_control_1_recovery_o, frontend_control_1_recovery_pc_o, stack_unit_1_p8, stack_unit_1_p9,
       stack_unit_1_p12, stack_unit_1_p17, stack_unit_1_p18, stack_unit_1_p20, stack_unit_1_p21,
       stack_unit_1_p22, stack_unit_1_p24, stack_unit_1_p27, stack_unit_1_p28, system_1_redirect_pc_o,
       system_1_sync_copile_o, undriven_3;

  fetch fetch_1 (
    .predict_pc_i(decode_predict_1_predict_pc_o), .decode_stop_i(decode_predict_1_stop_o),
    .consume_i(decode_predict_1_consume_o), .window_count_o(fetch_1_window_count_o),
    .window_o(fetch_1_window_o), .recovery_valid_i(frontend_control_1_recovery_valid_o),
    .halt_i(system_1_halted_o), .recovery_pc_i(frontend_control_1_recovery_pc_o),
    .window_fault_o(fetch_1_window_fault_o), .window_pc_o(fetch_1_window_pc_o),
    .consumed_bytes_i(decode_predict_1_consumed_bytes_o), .predict_valid_i(decode_predict_1_predict_valid_o));  // open: i_fault_i, i_ready_i, reset_i, clk_i, icache_invalidate_i, i_req_o, i_rvalid_i, i_addr_o, i_rdata_i
  decode_predict decode_predict_1 (
    .consume_o(decode_predict_1_consume_o), .window_count_i(fetch_1_window_count_o),
    .window_i(fetch_1_window_o), .recovery_i(frontend_control_1_recovery_o),
    .retire_i(frontend_control_1_retire_o), .window_fault_i(fetch_1_window_fault_o),
    .window_pc_i(fetch_1_window_pc_o), .consumed_bytes_o(decode_predict_1_consumed_bytes_o),
    .stop_o(decode_predict_1_stop_o), .predict_valid_o(decode_predict_1_predict_valid_o),
    .predict_pc_o(decode_predict_1_predict_pc_o), .out_ready_i(decode_queue_1_push_ready_o),
    .out_valid_o(decode_predict_1_out_valid_o), .out_count_o(decode_predict_1_out_count_o),
    .out_block_o(decode_predict_1_out_block_o));  // open: reset_i, clk_i
  // data_cache data_cache_1: pin names not known; wires that end beside it: data_cache_1_p1, data_cache_1_p2, data_cache_1_p3, data_cache_1_p4, data_cache_1_p5, data_cache_1_p6
  exec_arith exec_arith_1 (
    .sync_valid_i(stack_unit_1_p29), .issue_c_i(stack_unit_1_p8), .issue_b_i(stack_unit_1_p8),
    .issue_a_i(stack_unit_1_p8), .issue_op_i(stack_unit_1_p8), .issue_class_i(stack_unit_1_p8),
    .issue_valid_i(stack_unit_1_p6), .ready_o(exec_arith_1_ready_o),
    .complete_valid_o(exec_arith_1_complete_valid_o),
    .complete_result_valid_o(exec_arith_1_complete_valid_o),
    .complete_result_o(exec_arith_1_complete_valid_o), .complete_fault_o(exec_arith_1_complete_valid_o));  // open: clk_i, reset_i
  decode_queue decode_queue_1 (
    .push_count_i(decode_predict_1_out_count_o), .push_ready_o(decode_queue_1_push_ready_o),
    .push_valid_i(decode_predict_1_out_valid_o), .push_block_i(decode_predict_1_out_block_o),
    .flush_i(frontend_control_1_recovery_valid_o), .pop_take_i(stack_unit_1_p1),
    .pop_slot_o(decode_queue_1_pop_slot_o));  // open: reset_i, clk_i
  // stack_unit stack_unit_1: pin names not known; wires that end beside it: stack_unit_1_p1, decode_queue_1_pop_slot_o, data_cache_1_p1, data_cache_1_p2, data_cache_1_p3, stack_unit_1_p6, stack_unit_1_p7, stack_unit_1_p8, stack_unit_1_p9, stack_unit_1_p10, stack_unit_1_p11, stack_unit_1_p12, stack_unit_1_p13, stack_unit_1_p13, stack_unit_1_p15, stack_unit_1_p15, stack_unit_1_p17, stack_unit_1_p18, stack_unit_1_p19, stack_unit_1_p20, stack_unit_1_p21, stack_unit_1_p22, stack_unit_1_p22, stack_unit_1_p24, stack_unit_1_p25, stack_unit_1_p26, stack_unit_1_p27, stack_unit_1_p28, stack_unit_1_p29
  exec_entier exec_entier_1 (
    .arith_ready_i(exec_arith_1_ready_o), .stack_maint_done_i(undriven_2), .stack_maint_o(stack_unit_1_p21),
    .disp_i(stack_unit_1_p20), .disp_sel_o(stack_unit_1_p19), .frame_rsp_i(stack_unit_1_p18),
    .frame_dsp_i(stack_unit_1_p17), .complete_o(stack_unit_1_p12), .sync_valid_i(stack_unit_1_p29),
    .issue_i(stack_unit_1_p8), .issue_ready_o(stack_unit_1_p7), .issue_valid_i(stack_unit_1_p6),
    .arith_complete_(exec_arith_1_complete_valid_o), .limits_i(stack_unit_1_p22),
    .copile_o(exec_entier_1_copile_o), .sync_copile_i(system_1_sync_copile_o), .mem_req_o(data_cache_1_p6),
    .mem_ready_i(data_cache_1_p5), .mem_rsp_i(data_cache_1_p4));  // open: clk_i, reset_i
  frontend_control frontend_control_1 (
    .redirect_pc_i(system_1_redirect_pc_o), .stack_idle_i(stack_unit_1_p10),
    .decode_slot_i(decode_queue_1_pop_slot_o), .recovery_o(frontend_control_1_recovery_o),
    .recovery_pc_o(frontend_control_1_recovery_pc_o), .recovery_valid_o(frontend_control_1_recovery_valid_o),
    .retire_o(frontend_control_1_retire_o), .commit_i(stack_unit_1_p9), .redirect_valid_i(undriven),
    .boundary_valid_o(frontend_control_1_boundary_valid_o), .boundary_pc_o(frontend_control_1_boundary_pc_o));
  system system_1 (
    .halted_o(system_1_halted_o), .mem_rsp_i(data_cache_1_p4), .mem_ready_i(data_cache_1_p5),
    .mem_req_o(data_cache_1_p6), .sync_copile_o(system_1_sync_copile_o), .copile_i(exec_entier_1_copile_o),
    .limits_o(stack_unit_1_p22), .redirect_pc_o(system_1_redirect_pc_o), .redirect_valid_o(stack_unit_1_p11),
    .system_hold_o(system_1_system_hold_o), .boundary_pc_i(frontend_control_1_boundary_pc_o),
    .boundary_valid_i(frontend_control_1_boundary_valid_o), .fault_i(undriven_3), .fault_pc_i(undriven_3),
    .fault_valid_i(undriven_3), .disp_wdata_o(stack_unit_1_p24), .disp_wsel_o(stack_unit_1_p25),
    .disp_we_o(stack_unit_1_p26), .sync_rsp_o(stack_unit_1_p27), .sync_dsp_o(stack_unit_1_p28),
    .sync_valid_o(stack_unit_1_p29), .stack_maint_done_i(undriven_2), .complete_o(stack_unit_1_p12),
    .frame_dsp_i(stack_unit_1_p17), .frame_rsp_i(stack_unit_1_p18), .disp_sel_o(stack_unit_1_p19),
    .disp_i(stack_unit_1_p20), .stack_maint_o(stack_unit_1_p21), .issue_i(stack_unit_1_p8),
    .issue_ready_o(stack_unit_1_p7), .issue_valid_i(stack_unit_1_p6));  // open: resume_pc_i, resume_req_i, halt_cause_o, halt_req_i, irq_ack_code_o, irq_ack_o, irq_pending_i, boot_block_i, clk_i, reset_i, halt_pc_o, exit_code_o, fpc_o, fcode_o, dr_o

  // Notes on the sheet:
  //   32
  //   32
  //   6
  //   32
  //   6
  //   32
  //   256
  //   32
  //   6
  //   32
  //   6
  //   32
  //   256
  //   52
  //   3
  //   22
  //   8
  //   4
  //   572
  //   4
  //   572
  //   64
  //   64
  //   64
  //   143
  //   9
  //   64
  //   3
  //   66
  //   101
  //   66
  //   102
  //   75
  //   3
  //   143
  //   66
  //   101
  //   32
  //   22
  //   52
  //   143
  //   439
  //   439
  //   186
  //   186
  //   32
  //   102
  //   32
  //   108
  //   66
  //   32
  //   108
  //   32
  //   4
  //   32
  //   131
  //   193
  //   256
  //   32
  //   32
  //   4
  //   32
  //   131
  //   193
  //   64
  //   66
  //   102
  //   140
  //   108
  //   193
  //   256
  //   32
  //   32
  //   4
  //   32
  //   131
  //   193
  //   32
  //   4
  //   32
  //   32
  //   64
  //   32
  //   32
  //   4
  //   32
  //   32
  //   9
  //   32
  //   32
endmodule

module fetch (
  input  reset_i,
  input  clk_i,
  input  halt_i,
  input  icache_invalidate_i,
  input  recovery_valid_i,
  input  [31:0] recovery_pc_i,
  input  consume_i,
  input  [5:0] consumed_bytes_i,
  input  decode_stop_i,
  input  predict_valid_i,
  input  [31:0] predict_pc_i,
  input  i_ready_i,
  input  i_rvalid_i,
  input  i_fault_i,
  input  i_rdata_i,
  output [31:0] window_o,
  output [31:0] window_fault_o,
  output [5:0] window_count_o,
  output [31:0] window_pc_o,
  output i_req_o,
  output i_addr_o
);
endmodule

module decode_predict (
  input  [31:0] recovery_i,
  input  [21:0] retire_i,
  input  reset_i,
  input  clk_i,
  input  [31:0] window_i,
  input  [31:0] window_fault_i,
  input  [5:0] window_count_i,
  input  [31:0] window_pc_i,
  input  out_ready_i,
  output consume_o,
  output [5:0] consumed_bytes_o,
  output stop_o,
  output predict_valid_o,
  output [31:0] predict_pc_o,
  output out_valid_o,
  output [3:0] out_count_o,
  output [31:0] out_block_o
);
endmodule

module decode_queue (
  input  reset_i,
  input  clk_i,
  input  push_valid_i,
  input  [3:0] push_count_i,
  input  [31:0] push_block_i,
  input  flush_i,
  input  pop_take_i,
  output push_ready_o,
  output [31:0] pop_slot_o
);
endmodule

module stack_unit (
  input  reset_i,
  input  sync_valid_i,
  input  clk_i,
  input  [31:0] sync_dsp_i,
  input  issue_ready_i,
  input  [31:0] sync_rsp_i,
  input  disp_we_i,
  input  [31:0] complete_i,
  input  [31:0] decode_slot_i,
  input  [31:0] lim_dsp_i,
  input  [3:0] disp_wsel_i,
  input  decode_valid_i,
  input  [31:0] lim_rsp_i,
  input  [31:0] disp_wdata_i,
  input  [3:0] disp_sel_i,
  input  [31:0] maint_i,
  input  mem_ready_i,
  input  [31:0] mem_rsp_i,
  output issue_valid_o,
  output [31:0] issue_o,
  output decode_take_o,
  output [31:0] disp_o,
  output [31:0] commit_o,
  output idle_o,
  output [31:0] frame_rsp_o,
  output [31:0] frame_dsp_o,
  output maint_done_o,
  output [31:0] mem_req_o
);
endmodule

module data_cache (
  input  d_ready_i,
  input  d_rvalid_i,
  input  d_rdata_i,
  input  d_fault_i,
  input  reset_i,
  input  clk_i,
  input  [31:0] stack_req_i,
  input  [31:0] exec_req_i,
  output d_req_o,
  output d_write_o,
  output d_addr_o,
  output d_wdata_o,
  output stack_ready_o,
  output [31:0] stack_rsp_o,
  output exec_ready_o,
  output [31:0] exec_rsp_o
);
endmodule

module exec_entier (
  input  reset_i,
  input  [31:0] frame_dsp_i,
  input  [31:0] issue_i,
  input  clk_i,
  input  issue_valid_i,
  input  [31:0] disp_i,
  input  [31:0] frame_rsp_i,
  input  [31:0] mem_rsp_i,
  input  [31:0] arith_complete_,
  input  stack_maint_done_i,
  input  [2:0] arith_ready_i,
  input  mem_ready_i,
  input  [31:0] sync_copile_i,
  input  [31:0] limits_i,
  input  sync_valid_i,
  output [31:0] complete_o,
  output issue_ready_o,
  output [31:0] stack_maint_o,
  output [3:0] disp_sel_o,
  output [31:0] copile_o,
  output [31:0] mem_req_o
);
endmodule

module exec_arith (
  input  reset_i,
  input  clk_i,
  input  sync_valid_i,
  input  issue_valid_i,
  input  [31:0] issue_class_i,
  input  [31:0] issue_op_i,
  input  [31:0] issue_a_i,
  input  [31:0] issue_b_i,
  input  [31:0] issue_c_i,
  output [2:0] ready_o,
  output [31:0] complete_valid_o,
  output [31:0] complete_result_valid_o,
  output [31:0] complete_result_o,
  output [31:0] complete_fault_o
);
endmodule

module system (
  input  [31:0] resume_pc_i,
  input  reset_i,
  input  [31:0] boundary_pc_i,
  input  [31:0] mem_rsp_i,
  input  clk_i,
  input  issue_valid_i,
  input  [31:0] issue_i,
  input  [31:0] frame_dsp_i,
  input  mem_ready_i,
  input  [31:0] frame_rsp_i,
  input  [31:0] copile_i,
  input  [31:0] disp_i,
  input  boot_block_i,
  input  stack_maint_done_i,
  input  irq_pending_i,
  input  halt_req_i,
  input  resume_req_i,
  input  [31:0] fault_valid_i,
  input  [31:0] fault_i,
  input  [31:0] fault_pc_i,
  input  boundary_valid_i,
  output fcode_o,
  output system_hold_o,
  output dr_o,
  output redirect_valid_o,
  output [31:0] redirect_pc_o,
  output issue_ready_o,
  output [31:0] limits_o,
  output [31:0] complete_o,
  output [31:0] mem_req_o,
  output [31:0] sync_copile_o,
  output [3:0] disp_sel_o,
  output [31:0] stack_maint_o,
  output [31:0] sync_dsp_o,
  output sync_valid_o,
  output irq_ack_o,
  output irq_ack_code_o,
  output [3:0] disp_wsel_o,
  output disp_we_o,
  output halted_o,
  output [31:0] sync_rsp_o,
  output halt_cause_o,
  output [31:0] disp_wdata_o,
  output halt_pc_o,
  output exit_code_o,
  output fpc_o
);
endmodule

module frontend_control (
  input  [31:0] decode_slot_i,
  input  [31:0] commit_i,
  input  stack_idle_i,
  input  redirect_valid_i,
  input  [31:0] redirect_pc_i,
  output [31:0] recovery_pc_o,
  output recovery_valid_o,
  output [31:0] recovery_o,
  output [21:0] retire_o,
  output boundary_valid_o,
  output [31:0] boundary_pc_o
);
endmodule
